// Logisim project DisplayDriver.circ as structural Verilog: 1 circuit, main circuit main
module main (
);

  wire nor_1_out, nor_2_out, nor_3_out, nor_4_out, not_1_out, not_2_out, not_3_out, not_4_out, not_5_out;

  not not_1 (not_1_out, 1'b0);
  nor nor_1 (nor_1_out, 1'b0, 1'b0);
  nor nor_2 (nor_2_out, 1'b0, 1'b0);
  not not_2 (not_2_out, 1'b0);
  not not_3 (not_3_out, nor_1_out);
  not not_4 (not_4_out, nor_2_out);
  nor nor_3 (nor_3_out, not_2_out, 1'b0);
  nor nor_4 (nor_4_out, not_3_out, not_4_out);
  not not_5 (not_5_out, nor_3_out);
  _7_Segment_Display #(.active("false")) u_7_segment_display_1 (
    .g(not_5_out), .f(nor_4_out), .a(not_1_out), .b(1'b1), .e(nor_4_out), .d(nor_4_out), .c(1'b1), .dp(1'b1));

  // Notes on the sheet:
  //   a_o
  //   a_1
  //   a
  //   b
  //   c
  //   d,e,f
  //   g
endmodule
