// Logisim project PriorityEncoder.circ as structural Verilog: 1 circuit, main circuit main
module main (
);

  wire nor_1_out, nor_2_out, nor_3_out, nor_4_out, nor_5_out, not_1_out, not_2_out, not_3_out, undriven,
       undriven_2, undriven_3;

  not not_1 (not_1_out, undriven_2);
  not not_2 (not_2_out, undriven_3);
  nor nor_1 (nor_1_out, undriven, undriven_3);
  nor nor_2 (nor_2_out, undriven, not_1_out);
  nor nor_3 (nor_3_out, undriven_2, not_2_out);
  nor nor_4 (nor_4_out, nor_1_out, nor_2_out);
  not not_3 (not_3_out, nor_5_out);
  nor nor_5 (nor_5_out, nor_3_out, undriven);

  // Notes on the sheet:
  //   C
  //   L
  //   E
  //   a_0
  //   a_1
endmodule
