// Logisim project BCD-7SEG.circ as structural Verilog: 1 circuit, main circuit main
module main (
);

  wire button_1_out, button_2_out, n7_segment_display_driver_1_a_2, n7_segment_display_driver_1_b_2,
       n7_segment_display_driver_1_c_2, n7_segment_display_driver_1_d_2, n7_segment_display_driver_1_e,
       n7_segment_display_driver_1_f, n7_segment_display_driver_1_g;

  Button button_1 (.out(button_1_out));
  Button button_2 (.out(button_2_out));
  _7_segment_display_driver u_7_segment_display_driver_1 (
    .D(1'b0), .C(button_1_out), .B(1'b0), .A(button_2_out), .a_2(n7_segment_display_driver_1_a_2),
    .b_2(n7_segment_display_driver_1_b_2), .c_2(n7_segment_display_driver_1_c_2),
    .d_2(n7_segment_display_driver_1_d_2), .e(n7_segment_display_driver_1_e),
    .f(n7_segment_display_driver_1_f), .g(n7_segment_display_driver_1_g));
  _7_Segment_Display u_7_segment_display_1 (
    .g(n7_segment_display_driver_1_g), .f(n7_segment_display_driver_1_f),
    .a(n7_segment_display_driver_1_a_2), .b(n7_segment_display_driver_1_b_2),
    .e(n7_segment_display_driver_1_e), .d(n7_segment_display_driver_1_d_2),
    .c(n7_segment_display_driver_1_c_2));  // open: dp

  // Notes on the sheet:
  //   a1
  //   a0
endmodule
