// Logisim project BlackBox.circ as structural Verilog: 1 circuit, main circuit main
module main (
);

  wire button_1_out, button_2_out, button_3_out, button_4_out, nand_1_out, nand_2_out, nand_3_out,
       nand_4_out, nand_5_out, nand_6_out, nand_7_out, nand_8_out, not_1_out, not_2_out, not_3_out, not_4_out;

  Button button_1 (.out(button_1_out));
  Button button_2 (.out(button_2_out));
  Button button_3 (.out(button_3_out));
  Button button_4 (.out(button_4_out));
  not not_1 (not_1_out, button_4_out);
  not not_2 (not_2_out, button_2_out);
  not not_3 (not_3_out, button_3_out);
  nand nand_1 (nand_1_out, not_1_out, button_3_out);
  nand nand_2 (nand_2_out, button_4_out, button_2_out);
  nand nand_3 (nand_3_out, button_3_out, button_1_out);
  nand nand_4 (nand_4_out, not_2_out, not_3_out);
  nand nand_5 (nand_5_out, nand_1_out, nand_2_out);
  nand nand_6 (nand_6_out, nand_4_out, button_4_out);
  nand nand_7 (nand_7_out, button_1_out, nand_5_out);
  nand nand_8 (nand_8_out, nand_3_out, nand_6_out);
  not not_4 (not_4_out, nand_7_out);

  // Notes on the sheet:
  //   b0
  //   b1
  //   b2
  //   b3
  //   a1
  //   a0
endmodule
