// Logisim project prelab4.circ as structural Verilog: 1 circuit, main circuit main
module main (
);

  wire and_1_out, and_2_out, not_1_out, or_1_out, undriven, undriven_2, undriven_3, undriven_4, undriven_5,
       xor_1_out;

  and and_1 (and_1_out, undriven, undriven_2);
  or or_1 (or_1_out, and_1_out, undriven_3);
  xor xor_1 (xor_1_out, undriven_4, undriven_5);
  not not_1 (not_1_out, or_1_out);
  and and_2 (and_2_out, not_1_out, xor_1_out);

  // Notes on the sheet:
  //   W
  //   X
  //   V
  //   Y
  //   Z
  //   W1
  //   OUT1
  //   OUT2
endmodule
