// Logisim project Final.circ as structural Verilog: 1 circuit, main circuit main
module main (
);

  wire nor_1_out, nor_2_out, nor_3_out, nor_4_out, nor_5_out, nor_6_out, nor_7_out, nor_8_out, nor_9_out,
       not_1_out, not_2_out, not_3_out, not_4_out, not_5_out, not_6_out, not_7_out, not_8_out, undriven,
       undriven_2, undriven_3;

  not not_1 (not_1_out, undriven_2);
  not not_2 (not_2_out, undriven_3);
  nor nor_1 (nor_1_out, undriven, undriven_3);
  nor nor_2 (nor_2_out, undriven, not_1_out);
  nor nor_3 (nor_3_out, undriven_2, not_2_out);
  nor nor_4 (nor_4_out, nor_3_out, undriven);
  nor nor_5 (nor_5_out, nor_1_out, nor_2_out);
  not not_3 (not_3_out, nor_4_out);
  nor nor_6 (nor_6_out, nor_5_out, nor_5_out);
  nor nor_7 (nor_7_out, not_3_out, not_3_out);
  not not_4 (not_4_out, nor_5_out);
  not not_5 (not_5_out, nor_5_out);
  not not_6 (not_6_out, nor_6_out);
  not not_7 (not_7_out, nor_7_out);
  nor nor_8 (nor_8_out, not_4_out, not_3_out);
  nor nor_9 (nor_9_out, not_6_out, not_7_out);
  not not_8 (not_8_out, nor_8_out);
  _7_Segment_Display #(.active("false")) u_7_segment_display_1 (
    .g(not_8_out), .f(nor_9_out), .a(not_5_out), .b(1'b1), .e(nor_9_out), .d(nor_9_out), .c(1'b1), .dp(1'b1));

  // Notes on the sheet:
  //   C
  //   E
  //   L
  //   +5v
  //   a
  //   b
  //   c
  //   d,e,f
  //   g
endmodule
